# Fritzing sketch ESQUEMATICO_PROTO (saved by Fritzing 0.9.10b)
breadboards: 1

parts:
  Mod1 = Amica NodeMCU DEVKIT 1.0
  DHT1 = DHT11 Humitidy and Temperature Sensor
  GY-NEO6MV3 = SUP500F [package=sup500f]

nets:
  VDD: Mod1.pin1, Mod1.pin_10, Mod1.pin_26, DHT1.VDD, GY-NEO6MV3.VCC
  N1: Mod1.pin2, Mod1.pin_9, Mod1.pin_25, Mod1.pin_29, GY-NEO6MV3.TX-O
  N2: Mod1.pin6, GY-NEO6MV3.RX-I
  N3: Mod1.pin7, GY-NEO6MV3.GND
  N4: Mod1.pin_24, DHT1.NULL

notes:
  GND: Black
  VCC: Red
  RX: Yellow
  TX: BLUE

custom parts:
  DHT11 Humitidy and Temperature Sensor: DHT11 Humidity and Temperature Sensor
